// Logisim project ALU-TP-Vide.circ as structural Verilog
module Add (
  input  in_1,
  input  in_2,
  input  in_3,
  output out_4,
  output out_5
);

  wire and_1_out, and_2_out, and_3_out;

  and and_1 (and_1_out, in_1, in_2);
  and and_2 (and_2_out, in_1, in_3);
  and and_3 (and_3_out, in_2, in_3);
  xor xor_1 (out_4, in_1, in_2, in_3);
  or or_1 (out_5, and_1_out, and_2_out, and_3_out);
endmodule

module Add4 (
  input  in_1,
  input  in_2,
  input  in_3,
  input  in_4,
  input  in_5,
  input  in_6,
  input  in_7,
  input  in_8,
  input  in_9,
  output out_10,
  output out_11,
  output out_12,
  output out_13,
  output out_14
);

  wire add_2_out_5, add_3_out_5, add_4_out_5;

  Add add_1 (.in_1(in_1), .in_2(in_5), .in_3(add_3_out_5), .out_4(out_11), .out_5(out_10));
  Add add_2 (.in_1(in_3), .in_2(in_7), .in_3(add_4_out_5), .out_4(out_13), .out_5(add_2_out_5));
  Add add_3 (.in_1(in_2), .in_2(in_6), .in_3(add_2_out_5), .out_4(out_12), .out_5(add_3_out_5));
  Add add_4 (.in_1(in_4), .in_2(in_8), .in_3(in_9), .out_4(out_14), .out_5(add_4_out_5));
endmodule

module Sub4 (
  input  in_1,
  input  in_2,
  input  in_3,
  input  in_4,
  input  in_5,
  input  in_6,
  input  in_7,
  input  in_8,
  input  in_9,
  output out_10,
  output out_11,
  output out_12,
  output out_13,
  output out_14
);

  wire exo1_1_out_5, exo1_1_out_6, exo1_1_out_7, exo1_1_out_8;

  Add4 add4_1 (
    .out_10(out_10), .in_9(in_9), .in_1(in_1), .in_5(exo1_1_out_5), .in_2(in_2), .in_6(exo1_1_out_6),
    .in_3(in_3), .in_7(exo1_1_out_7), .in_4(in_4), .in_8(exo1_1_out_8), .out_11(out_11), .out_12(out_12),
    .out_13(out_13), .out_14(out_14));
  Exo1 exo1_1 (
    .in_1(in_8), .in_2(in_7), .in_3(in_6), .in_4(in_5), .out_5(exo1_1_out_5), .out_6(exo1_1_out_6),
    .out_7(exo1_1_out_7), .out_8(exo1_1_out_8));
endmodule

module Mul4_8 (
  input  in_1,
  input  in_2,
  input  in_3,
  input  in_4,
  input  in_5,
  input  in_6,
  input  in_7,
  input  in_8,
  output out_9,
  output out_10,
  output out_11,
  output out_12,
  output out_13,
  output out_14,
  output out_15,
  output out_16
);

  wire add4_1_out_10, add4_1_out_11, add4_1_out_12, add4_1_out_13, add4_2_out_10, add4_2_out_11,
       add4_2_out_12, add4_2_out_13, mult_1_out_6, mult_1_out_7, mult_1_out_8, mult_2_out_6, mult_2_out_7,
       mult_2_out_8, mult_2_out_9, mult_3_out_6, mult_3_out_7, mult_3_out_8, mult_3_out_9, mult_4_out_6,
       mult_4_out_7, mult_4_out_8, mult_4_out_9;

  Mult mult_1 (
    .in_1(in_4), .in_2(in_5), .in_3(in_6), .in_4(in_7), .in_5(in_8), .out_6(mult_1_out_6),
    .out_7(mult_1_out_7), .out_8(mult_1_out_8), .out_9(out_9));
  Mult mult_2 (
    .in_1(in_3), .in_2(in_5), .in_3(in_6), .in_4(in_7), .in_5(in_8), .out_6(mult_2_out_6),
    .out_7(mult_2_out_7), .out_8(mult_2_out_8), .out_9(mult_2_out_9));
  Mult mult_3 (
    .in_1(in_2), .in_2(in_5), .in_3(in_6), .in_4(in_7), .in_5(in_8), .out_6(mult_3_out_6),
    .out_7(mult_3_out_7), .out_8(mult_3_out_8), .out_9(mult_3_out_9));
  Mult mult_4 (
    .in_1(in_1), .in_2(in_5), .in_3(in_6), .in_4(in_7), .in_5(in_8), .out_6(mult_4_out_6),
    .out_7(mult_4_out_7), .out_8(mult_4_out_8), .out_9(mult_4_out_9));
  Add4 add4_1 (
    .out_10(add4_1_out_10), .in_9(1'b0), .in_1(mult_2_out_6), .in_5(1'b0), .in_2(mult_2_out_7),
    .in_6(mult_1_out_6), .in_3(mult_2_out_8), .in_7(mult_1_out_7), .in_4(mult_2_out_9), .in_8(mult_1_out_8),
    .out_11(add4_1_out_11), .out_12(add4_1_out_12), .out_13(add4_1_out_13), .out_14(out_10));
  Add4 add4_2 (
    .out_10(add4_2_out_10), .in_9(add4_1_out_10), .in_1(mult_3_out_6), .in_5(1'b0), .in_2(mult_3_out_7),
    .in_6(add4_1_out_11), .in_3(mult_3_out_8), .in_7(add4_1_out_12), .in_4(mult_3_out_9),
    .in_8(add4_1_out_13), .out_11(add4_2_out_11), .out_12(add4_2_out_12), .out_13(add4_2_out_13),
    .out_14(out_11));
  Add4 add4_3 (
    .out_10(out_16), .in_9(add4_2_out_10), .in_1(mult_4_out_6), .in_5(1'b0), .in_2(mult_4_out_7),
    .in_6(add4_2_out_11), .in_3(mult_4_out_8), .in_7(add4_2_out_12), .in_4(mult_4_out_9),
    .in_8(add4_2_out_13), .out_11(out_15), .out_12(out_14), .out_13(out_13), .out_14(out_12));
endmodule

module ALU (
  input  in_1,
  input  in_2,
  input  in_3,
  input  in_4,
  input  in_5,
  input  in_6,
  input  in_7,
  input  in_8,
  output out_9,
  output out_10,
  output out_11,
  output out_12,
  output out_13,
  output out_14,
  output out_15,
  output out_16
);

  Mul4_8 mul4_8_1 (
    .in_1(in_1), .in_2(in_2), .in_3(in_3), .in_4(in_4), .in_5(in_5), .in_6(in_6), .in_7(in_4), .in_8(in_8));  // open: out_9, out_10, out_11, out_12, out_13, out_14, out_15, out_16
  Sub4 sub4_1 (
    .in_9(1'b0), .in_1(in_1), .in_2(in_2), .in_3(in_3), .in_4(in_4), .in_5(in_5), .in_6(in_6), .in_7(in_4),
    .in_8(in_8));  // open: out_10, out_11, out_12, out_13, out_14
  Add4 add4_1 (
    .in_9(1'b0), .in_1(in_1), .in_5(in_5), .in_2(in_2), .in_6(in_6), .in_3(in_3), .in_7(in_4), .in_4(in_4),
    .in_8(in_8));  // open: out_10, out_11, out_12, out_13, out_14
  Multiplexer #(.select(3), .width(8)) multiplexer_1 ();  // open: in0, in1, in2, in3, in4, in5, in6, in7, out, sel, en
  // OR_Gate or_1 has open pins: out=out_9
  // OR_Gate or_2 has open pins: out=out_10
  // OR_Gate or_3 has open pins: out=out_11
  // OR_Gate or_4 has open pins: out=out_12
  // OR_Gate or_5 has open pins: out=out_13
  // OR_Gate or_6 has open pins: out=out_14
  // OR_Gate or_7 has open pins: out=out_15
  // OR_Gate or_8 has open pins: out=out_16

  assign in_7 = in_4;
endmodule

module Add4_exemple (
  input  in_1,
  input  in_2,
  input  in_3,
  input  in_4,
  input  in_5,
  input  in_6,
  input  in_7,
  input  in_8,
  input  in_9,
  output out_10
);

  wire afficheur_1_a, afficheur_1_b, afficheur_1_c, afficheur_1_d, afficheur_1_e, afficheur_1_f,
       afficheur_1_g, afficheur_1_m, afficheur_2_a, afficheur_2_b, afficheur_2_c, afficheur_2_d,
       afficheur_2_e, afficheur_2_f, afficheur_2_g, afficheur_2_m, afficheur_3_a, afficheur_3_b,
       afficheur_3_c, afficheur_3_d, afficheur_3_e, afficheur_3_f, afficheur_3_g, afficheur_3_m;
  wire [3:0] add4_1_out_14;

  Afficheur afficheur_1 (
    .b3(in_1), .b2(in_3), .b1(in_5), .b0(in_7), .a(afficheur_1_a), .b(afficheur_1_b), .c(afficheur_1_c),
    .d(afficheur_1_d), .e(afficheur_1_e), .f(afficheur_1_f), .g(afficheur_1_g), .m(afficheur_1_m));
  _7_Segment_Display u_7_segment_display_1 (.g(afficheur_1_m));  // open: f, a, b, e, d, c, dp
  _7_Segment_Display u_7_segment_display_2 (
    .g(afficheur_1_g), .f(afficheur_1_f), .a(afficheur_1_a), .b(afficheur_1_b), .e(afficheur_1_e),
    .d(afficheur_1_d), .c(afficheur_1_c));  // open: dp
  Add4 add4_1 (
    .out_10(out_10), .in_9(in_9), .in_1(in_1), .in_5(in_2), .in_2(in_3), .in_6(in_4), .in_3(in_5),
    .in_7(in_6), .in_4(in_7), .in_8(in_8), .out_11(add4_1_out_14[3]), .out_12(add4_1_out_14[2]),
    .out_13(add4_1_out_14[1]), .out_14(add4_1_out_14[0]));
  Afficheur afficheur_2 (
    .b3(add4_1_out_14[3]), .b2(add4_1_out_14[2]), .b1(add4_1_out_14[1]), .b0(add4_1_out_14[0]),
    .a(afficheur_2_a), .b(afficheur_2_b), .c(afficheur_2_c), .d(afficheur_2_d), .e(afficheur_2_e),
    .f(afficheur_2_f), .g(afficheur_2_g), .m(afficheur_2_m));
  _7_Segment_Display u_7_segment_display_3 (.g(afficheur_2_m));  // open: f, a, b, e, d, c, dp
  Afficheur afficheur_3 (
    .b3(in_2), .b2(in_4), .b1(in_6), .b0(in_8), .a(afficheur_3_a), .b(afficheur_3_b), .c(afficheur_3_c),
    .d(afficheur_3_d), .e(afficheur_3_e), .f(afficheur_3_f), .g(afficheur_3_g), .m(afficheur_3_m));
  _7_Segment_Display u_7_segment_display_4 (.g(afficheur_3_m));  // open: f, a, b, e, d, c, dp
  _7_Segment_Display u_7_segment_display_5 (
    .g(afficheur_2_g), .f(afficheur_2_f), .a(afficheur_2_a), .b(afficheur_2_b), .e(afficheur_2_e),
    .d(afficheur_2_d), .c(afficheur_2_c));  // open: dp
  _7_Segment_Display u_7_segment_display_6 (
    .g(afficheur_3_g), .f(afficheur_3_f), .a(afficheur_3_a), .b(afficheur_3_b), .e(afficheur_3_e),
    .d(afficheur_3_d), .c(afficheur_3_c));  // open: dp
endmodule

module Afficheur (
  input  b3,
  input  b2,
  input  b1,
  input  b0,
  output a,
  output b,
  output c,
  output d,
  output e,
  output f,
  output g,
  output m
);

  wire and_1_out, and_2_out, and_3_out, and_4_out, and_5_out, and_6_out, and_7_out, and_8_out, and_9_out,
       and_10_out, and_11_out, and_12_out, and_13_out, and_14_out, and_15_out, and_16_out, and_17_out,
       and_18_out, and_19_out, and_20_out, and_21_out, and_22_out, and_23_out, and_24_out, and_25_out,
       and_26_out, and_27_out, not_1_out, not_2_out, not_3_out, not_4_out, not_5_out, not_6_out, not_7_out,
       not_8_out, not_9_out, not_10_out, not_11_out, not_12_out, not_13_out, not_14_out, not_15_out,
       not_16_out, not_17_out, not_18_out, not_19_out, not_20_out, not_21_out, not_22_out, not_23_out,
       not_24_out, not_25_out, not_26_out, not_27_out, not_28_out, not_29_out, not_30_out, not_31_out,
       not_32_out, not_33_out, not_34_out, not_35_out, not_36_out, not_37_out, not_38_out;

  not not_1 (not_1_out, b3);
  not not_2 (not_2_out, b2);
  not not_3 (not_3_out, b0);
  not not_4 (not_4_out, b2);
  not not_5 (not_5_out, b3);
  not not_6 (not_6_out, b1);
  not not_7 (not_7_out, b2);
  not not_8 (not_8_out, b1);
  not not_9 (not_9_out, b0);
  not not_10 (not_10_out, b3);
  and and_1 (and_1_out, not_10_out, not_11_out);
  not not_11 (not_11_out, b2);
  not not_12 (not_12_out, b2);
  and and_2 (and_2_out, not_12_out, not_13_out);
  not not_13 (not_13_out, b1);
  not not_14 (not_14_out, b1);
  and and_3 (and_3_out, not_14_out, not_15_out);
  not not_15 (not_15_out, b0);
  not not_16 (not_16_out, b3);
  and and_4 (and_4_out, not_16_out, b1, b0);
  and and_5 (and_5_out, b3, b2);
  not not_17 (not_17_out, b1);
  not not_18 (not_18_out, b3);
  and and_6 (and_6_out, not_18_out, b2);
  and and_7 (and_7_out, b3, not_19_out);
  not not_19 (not_19_out, b2);
  not not_20 (not_20_out, b2);
  and and_8 (and_8_out, not_20_out, not_21_out);
  not not_21 (not_21_out, b0);
  not not_22 (not_22_out, b2);
  and and_9 (and_9_out, not_22_out, b1);
  and and_10 (and_10_out, b1, not_23_out);
  not not_23 (not_23_out, b0);
  not not_24 (not_24_out, b1);
  and and_11 (and_11_out, b2, not_24_out, b0);
  not not_25 (not_25_out, b2);
  and and_12 (and_12_out, not_25_out, not_26_out);
  not not_26 (not_26_out, b0);
  and and_13 (and_13_out, b1, not_27_out);
  not not_27 (not_27_out, b0);
  not not_28 (not_28_out, b1);
  and and_14 (and_14_out, not_28_out, not_29_out);
  not not_29 (not_29_out, b0);
  not not_30 (not_30_out, b3);
  and and_15 (and_15_out, not_30_out, b2, not_31_out);
  not not_31 (not_31_out, b1);
  not not_32 (not_32_out, b3);
  and and_16 (and_16_out, not_32_out, b2, not_33_out);
  not not_33 (not_33_out, b0);
  and and_17 (and_17_out, b3, not_34_out, b1);
  not not_34 (not_34_out, b2);
  not not_35 (not_35_out, b2);
  and and_18 (and_18_out, not_35_out, b1);
  and and_19 (and_19_out, b1, not_36_out);
  not not_36 (not_36_out, b0);
  and and_20 (and_20_out, b2, not_37_out);
  not not_37 (not_37_out, b1);
  and and_21 (and_21_out, b3, not_38_out);
  not not_38 (not_38_out, b0);
  and and_22 (and_22_out, not_1_out, not_2_out, not_3_out);
  and and_23 (and_23_out, not_4_out, b1, b0);
  and and_24 (and_24_out, not_5_out, b2, b0);
  and and_25 (and_25_out, b2, not_6_out, b0);
  and and_26 (and_26_out, b3, not_7_out, not_8_out);
  and and_27 (and_27_out, b3, b2, b1, not_9_out);
  or or_1 (b, and_1_out, and_2_out, and_3_out, and_4_out, and_5_out);
  or or_2 (c, not_17_out, b0, and_6_out, and_7_out);
  or or_3 (d, and_8_out, and_9_out, and_10_out, and_11_out);
  or or_4 (e, and_12_out, and_13_out);
  or or_5 (f, and_14_out, and_15_out, and_16_out, and_17_out);
  or or_6 (g, and_18_out, and_19_out, and_20_out, and_21_out);
  or or_7 (a, and_22_out, and_23_out, and_24_out, and_25_out, and_26_out, and_27_out);

  assign m = b3;
endmodule

module Exo1 (
  input  in_1,
  input  in_2,
  input  in_3,
  input  in_4,
  output out_5,
  output out_6,
  output out_7,
  output out_8
);

  wire not_1_out, not_2_out, not_3_out, not_4_out;

  not not_1 (not_1_out, in_1);
  not not_2 (not_2_out, in_2);
  not not_3 (not_3_out, in_3);
  not not_4 (not_4_out, in_4);
  Add4 add4_1 (
    .in_9(1'b1), .in_1(not_4_out), .in_5(1'b0), .in_2(not_3_out), .in_6(1'b0), .in_3(not_2_out), .in_7(1'b0),
    .in_4(not_1_out), .in_8(1'b0), .out_11(out_5), .out_12(out_6), .out_13(out_7), .out_14(out_8));  // open: out_10
endmodule

module Mult (
  input  in_1,
  input  in_2,
  input  in_3,
  input  in_4,
  input  in_5,
  output out_6,
  output out_7,
  output out_8,
  output out_9
);

  and and_1 (out_6, in_1, in_2);
  and and_2 (out_7, in_1, in_3);
  and and_3 (out_9, in_1, in_5);
  and and_4 (out_8, in_1, in_4);
endmodule
